// Logisim project Project3main.circ as structural Verilog: 7 circuits, main circuit CPU15
module main (
  input  Enable_Breakpoint
);

  wire chipset_1_irq, CLK, clock_1_out, cpu15_1_c, cpu15_1_e, cpu15_1_i, cpu15_1_n, cpu15_1_o, cpu15_1_z,
       KBCLR, KBIRQ, KBRD, MEMCS, nand_1_out, RE, TTYCLR, TTYWE, WE;
  wire [6:0] KBDATA, TTYDATA;
  wire [7:0] cpu15_1_srf;
  wire [14:0] ADDR, chipset_1_ivect, chipset_1_led0, chipset_1_led1, chipset_1_led2, chipset_1_led3,
       chipset_1_led4, chipset_1_led5, chipset_1_led6, chipset_1_led7, chipset_1_led8, chipset_1_led9,
       chipset_1_leda, chipset_1_ledb, chipset_1_ledc, chipset_1_ledd, chipset_1_lede, cpu15_1_ib,
       cpu15_1_pc, cpu15_1_r0, cpu15_1_r1, cpu15_1_r2, cpu15_1_r3, cpu15_1_r4, cpu15_1_r5, cpu15_1_r6,
       cpu15_1_r7, cpu15_1_srp, DATA, xnor_1_out;

  Clock clock_1 (.out(clock_1_out));
  nand nand_1 (nand_1_out, Enable_Breakpoint, xnor_1_out[0], xnor_1_out[1], xnor_1_out[2], xnor_1_out[3], xnor_1_out[4], xnor_1_out[5], xnor_1_out[6], xnor_1_out[7], xnor_1_out[8], xnor_1_out[9], xnor_1_out[10], xnor_1_out[11], xnor_1_out[12], xnor_1_out[13], xnor_1_out[14], 1'b1);
  and and_1 (CLK, clock_1_out, nand_1_out);
  assign xnor_1_out = ~(15'h36 ^ cpu15_1_pc);  // XNOR_Gate xnor_1, 15 bits wide
  LED I (.in(cpu15_1_i));
  LED Z (.in(cpu15_1_z));
  LED N (.in(cpu15_1_n));
  LED O (.in(cpu15_1_o));
  LED C (.in(cpu15_1_c));
  LED E (.in(cpu15_1_e));
  // Probe on cpu15_1_pc
  // Probe on cpu15_1_ib
  // Probe on cpu15_1_srp
  // Probe on cpu15_1_srf
  // Probe on cpu15_1_r0
  // Probe on cpu15_1_r1
  // Probe on cpu15_1_r2
  // Probe on cpu15_1_r3
  // Probe on cpu15_1_r4
  // Probe on cpu15_1_r5
  // Probe on cpu15_1_r6
  // Probe on cpu15_1_r7
  CPU15 cpu15_1 (
    .I(cpu15_1_i), .Z(cpu15_1_z), .N(cpu15_1_n), .O(cpu15_1_o), .C(cpu15_1_c), .E(cpu15_1_e),
    .PC(cpu15_1_pc), .IB(cpu15_1_ib), .SRP(cpu15_1_srp), .SRF(cpu15_1_srf), .R0(cpu15_1_r0), .R1(cpu15_1_r1),
    .R2(cpu15_1_r2), .R3(cpu15_1_r3), .R4(cpu15_1_r4), .R5(cpu15_1_r5), .R6(cpu15_1_r6), .R7(cpu15_1_r7),
    .CLK(CLK), .IRQ(chipset_1_irq), .RE(RE), .WE(WE), .ADDR(ADDR), .DATAIN(DATA), .DATAOUT(DATA));
  // Probe on ADDR
  // Probe on DATA
  // Probe on chipset_1_ivect
  RAM #(.addrWidth(15), .dataWidth(15)) ram_1 (.addr(ADDR), .data(DATA), .sel(MEMCS), .clk(CLK), .ld(RE));  // open: clr
  // Probe on TTYDATA
  CHIPSET chipset_1 (
    .RE(RE), .WE(WE), .ADDR(ADDR), .CPUDATAIN(DATA), .CPUDATAOUT(DATA), .IRQ(chipset_1_irq),
    .IVECT(chipset_1_ivect), .CLK(CLK), .MEMCS(MEMCS), .TTYWR(TTYWE), .TTYCLR(TTYCLR), .TTYDATA(TTYDATA),
    .KBRD(KBRD), .KBCLR(KBCLR), .KBIRQ(KBIRQ), .KBDATA(KBDATA), .LED0(chipset_1_led0), .LED1(chipset_1_led1),
    .LED2(chipset_1_led2), .LED3(chipset_1_led3), .LED4(chipset_1_led4), .LED5(chipset_1_led5),
    .LED6(chipset_1_led6), .LED7(chipset_1_led7), .LED8(chipset_1_led8), .LED9(chipset_1_led9),
    .LEDA(chipset_1_leda), .LEDB(chipset_1_ledb), .LEDC(chipset_1_ledc), .LEDD(chipset_1_ledd),
    .LEDE(chipset_1_lede));
  TTY tty_1 (.data(TTYDATA), .clk(CLK), .we(TTYWE), .clr(TTYCLR));
  Keyboard keyboard_1 (.clk(CLK), .re(KBRD), .clr(KBCLR), .avail(KBIRQ), .data(KBDATA));
  DotMatrix #(.matrixcols(15), .matrixrows(15)) dotmatrix_1 (
    .col0(chipset_1_led0), .col1(chipset_1_led1), .col2(chipset_1_led2), .col3(chipset_1_led3),
    .col4(chipset_1_led4), .col5(chipset_1_led5), .col6(chipset_1_led6), .col7(chipset_1_led7),
    .col8(chipset_1_led8), .col9(chipset_1_led9), .col10(chipset_1_leda), .col11(chipset_1_ledb),
    .col12(chipset_1_ledc), .col13(chipset_1_ledd), .col14(chipset_1_lede));
endmodule

// CPU
module CPU15 (
  input  [14:0] DATAIN,
  input  CLK,
  input  IRQ,
  output [14:0] PC,
  output [14:0] IB,
  output [14:0] SRP,
  output [7:0] SRF,
  output [14:0] R0,
  output [14:0] R1,
  output [14:0] R2,
  output [14:0] R3,
  output [14:0] R4,
  output [14:0] R5,
  output [14:0] R6,
  output [14:0] R7,
  output RE,
  output WE,
  output I,
  output Z,
  output [14:0] ADDR,
  output N,
  output O,
  output C,
  output E,
  output [14:0] DATAOUT
);

  RegisterFile registerfile_1 ();  // open: A1, A2, WD, RD1, RD2, WE, A3, CLK

  // Other names for the same wires on the sheet: DATA[14:0] = DATAIN
endmodule

module CHIPSET (
  input  RE,
  input  WE,
  input  [14:0] ADDR,
  input  [14:0] CPUDATAIN,
  input  KBIRQ,
  input  [6:0] KBDATA,
  input  CLK,
  output MEMCS,
  output TTYWR,
  output [14:0] IVECT,
  output TTYCLR,
  output [6:0] TTYDATA,
  output KBRD,
  output KBCLR,
  output [14:0] CPUDATAOUT,
  output IRQ,
  output [14:0] LED0,
  output [14:0] LED1,
  output [14:0] LED2,
  output [14:0] LED3,
  output [14:0] LED4,
  output [14:0] LED5,
  output [14:0] LED6,
  output [14:0] LED7,
  output [14:0] LED8,
  output [14:0] LED9,
  output [14:0] LEDA,
  output [14:0] LEDB,
  output [14:0] LEDC,
  output [14:0] LEDD,
  output [14:0] LEDE
);

  wire and_1_out, and_8_out, and_10_out, DATA7, IOCS, IVECTADDR, IVECTEN, IVECTRE, KBCS, LED0EN, LED0END,
       LED1EN, LED1END, LED2EN, LED2END, LED3EN, LED3END, LED4EN, LED4END, LED5EN, LED5END, LED6EN, LED6END,
       LED7EN, LED7END, LED8EN, LED8END, LED9EN, LED9END, LEDAEN, LEDAEND, LEDBEN, LEDBEND, LEDCEN, LEDCEND,
       LEDCS, LEDDEN, LEDDEND, LEDEEN, LEDEEND, LEDFEND, LEDRE, multiplexer_17_out, multiplexer_18_out, RWE,
       TTYCS;
  wire [14:0] DATAL0, DATAL1, DATAL2, DATAL3, DATAL4, DATAL5, DATAL6, DATAL7, DATAL8, DATAL9, DATALA, DATALB,
       DATALC, DATALD, DATALE, LEDDATA;
  wire [14:8] KBDATA15;

  assign CPUDATAOUT = KBRD ? {KBDATA15, DATA7, KBDATA} : 15'bz;  // Controlled_Buffer controlled_buffer_1
  assign CPUDATAOUT = LEDRE ? LEDDATA : 15'bz;  // Controlled_Buffer controlled_buffer_2
  assign CPUDATAOUT = IVECTRE ? IVECT : 15'bz;  // Controlled_Buffer controlled_buffer_3
  Register #(.width(15)) register_1 (.D(DATAL0), .en(LED0EN), .Q(LED0), .clk(CLK));  // open: clr
  Register #(.width(15)) register_2 (.D(DATAL1), .en(LED1EN), .Q(LED1), .clk(CLK));  // open: clr
  Register #(.width(15)) register_3 (.D(DATAL2), .en(LED2EN), .Q(LED2), .clk(CLK));  // open: clr
  Register #(.width(15)) register_4 (.D(DATAL3), .en(LED3EN), .Q(LED3), .clk(CLK));  // open: clr
  Register #(.width(15)) register_5 (.D(DATAL4), .en(LED4EN), .Q(LED4), .clk(CLK));  // open: clr
  and and_1 (and_1_out, WE, LEDCS);
  Decoder #(.select(4), .disabled(0)) decoder_1 (
    .out0(LED0END), .out1(LED1END), .out2(LED2END), .out3(LED3END), .out4(LED4END), .out5(LED5END),
    .out6(LED6END), .out7(LED7END), .out8(LED8END), .out9(LED9END), .out10(LEDAEND), .out11(LEDBEND),
    .out12(LEDCEND), .out13(LEDDEND), .out14(LEDEEND), .out15(LEDFEND), .sel(ADDR[3:0]), .en(and_1_out));
  Register #(.width(15)) register_6 (.D(DATAL5), .en(LED5EN), .Q(LED5), .clk(CLK));  // open: clr
  Register #(.width(15)) register_7 (.D(DATAL6), .en(LED6EN), .Q(LED6), .clk(CLK));  // open: clr
  Register #(.width(15)) register_8 (.D(DATAL7), .en(LED7EN), .Q(LED7), .clk(CLK));  // open: clr
  Register #(.width(15)) register_9 (.D(DATAL8), .en(LED8EN), .Q(LED8), .clk(CLK));  // open: clr
  Register #(.width(15)) register_10 (.D(DATAL9), .en(LED9EN), .Q(LED9), .clk(CLK));  // open: clr
  or or_1 (LED0EN, LED0END, LEDFEND);
  or or_2 (LED1EN, LED1END, LEDFEND);
  or or_3 (LED2EN, LED2END, LEDFEND);
  or or_4 (LED3EN, LED3END, LEDFEND);
  or or_5 (LED4EN, LED4END, LEDFEND);
  or or_6 (LED5EN, LED5END, LEDFEND);
  or or_7 (LED6EN, LED6END, LEDFEND);
  or or_8 (LED7EN, LED7END, LEDFEND);
  or or_9 (LED8EN, LED8END, LEDFEND);
  or or_10 (LED9EN, LED9END, LEDFEND);
  or or_11 (LEDAEN, LEDAEND, LEDFEND);
  or or_12 (LEDBEN, LEDBEND, LEDFEND);
  or or_13 (LEDCEN, LEDCEND, LEDFEND);
  or or_14 (LEDDEN, LEDDEND, LEDFEND);
  or or_15 (LEDEEN, LEDEEND, LEDFEND);
  Pull_Resistor pull_resistor_1 (.node(KBDATA15[13]));
  Pull_Resistor pull_resistor_2 (.node(KBDATA15[14]));
  Pull_Resistor pull_resistor_3 (.node(KBDATA15[12]));
  Pull_Resistor pull_resistor_4 (.node(KBDATA15[11]));
  Pull_Resistor pull_resistor_5 (.node(KBDATA15[9]));
  Pull_Resistor pull_resistor_6 (.node(KBDATA15[10]));
  Pull_Resistor pull_resistor_7 (.node(KBDATA15[8]));
  Pull_Resistor pull_resistor_8 (.node(DATA7));
  Register #(.width(15)) register_11 (.D(DATALA), .en(LEDAEN), .Q(LEDA), .clk(CLK));  // open: clr
  Register #(.width(15)) register_12 (.D(DATALB), .en(LEDBEN), .Q(LEDB), .clk(CLK));  // open: clr
  Register #(.width(15)) register_13 (.D(DATALC), .en(LEDCEN), .Q(LEDC), .clk(CLK));  // open: clr
  Register #(.width(15)) register_14 (.D(DATALD), .en(LEDDEN), .Q(LEDD), .clk(CLK));  // open: clr
  Register #(.width(15)) register_15 (.D(DATALE), .en(LEDEEN), .Q(LEDE), .clk(CLK));  // open: clr
  Multiplexer #(.width(15), .enable("false")) multiplexer_1 (.in0(CPUDATAIN), .in1(LED1), .out(DATAL0), .sel(LEDFEND));
  Multiplexer #(.width(15), .enable("false")) multiplexer_2 (.in0(CPUDATAIN), .in1(LED2), .out(DATAL1), .sel(LEDFEND));
  Multiplexer #(.width(15), .enable("false")) multiplexer_3 (.in0(CPUDATAIN), .in1(LED3), .out(DATAL2), .sel(LEDFEND));
  Multiplexer #(.width(15), .enable("false")) multiplexer_4 (.in0(CPUDATAIN), .in1(LED4), .out(DATAL3), .sel(LEDFEND));
  Multiplexer #(.width(15), .enable("false")) multiplexer_5 (.in0(CPUDATAIN), .in1(LED5), .out(DATAL4), .sel(LEDFEND));
  Multiplexer #(.select(4), .width(15)) multiplexer_6 (
    .in0(LED0), .in1(LED1), .in2(LED2), .in3(LED3), .in4(LED4), .in5(LED5), .in6(LED6), .in7(LED7),
    .in8(LED8), .in9(LED9), .in10(LEDA), .in11(LEDB), .in12(LEDC), .in13(LEDD), .in14(LEDE),
    .in15({15{1'b0}}), .out(LEDDATA), .sel(ADDR[3:0]), .en(LEDRE));
  Multiplexer #(.width(15), .enable("false")) multiplexer_7 (.in0(CPUDATAIN), .in1(LED6), .out(DATAL5), .sel(LEDFEND));
  Multiplexer #(.width(15), .enable("false")) multiplexer_8 (.in0(CPUDATAIN), .in1(LED7), .out(DATAL6), .sel(LEDFEND));
  Multiplexer #(.width(15), .enable("false")) multiplexer_9 (.in0(CPUDATAIN), .in1(LED8), .out(DATAL7), .sel(LEDFEND));
  Multiplexer #(.width(15), .enable("false")) multiplexer_10 (.in0(CPUDATAIN), .in1(LED9), .out(DATAL8), .sel(LEDFEND));
  Multiplexer #(.width(15), .enable("false")) multiplexer_11 (.in0(CPUDATAIN), .in1(LEDA), .out(DATAL9), .sel(LEDFEND));
  and and_2 (LEDRE, RE, LEDCS);
  Multiplexer #(.width(15), .enable("false")) multiplexer_12 (.in0(CPUDATAIN), .in1(LEDB), .out(DATALA), .sel(LEDFEND));
  Multiplexer #(.width(15), .enable("false")) multiplexer_13 (.in0(CPUDATAIN), .in1(LEDC), .out(DATALB), .sel(LEDFEND));
  Multiplexer #(.width(15), .enable("false")) multiplexer_14 (.in0(CPUDATAIN), .in1(LEDD), .out(DATALC), .sel(LEDFEND));
  Multiplexer #(.width(15), .enable("false")) multiplexer_15 (.in0(CPUDATAIN), .in1(LEDE), .out(DATALD), .sel(LEDFEND));
  Multiplexer #(.width(15), .enable("false")) multiplexer_16 (
    .in0(CPUDATAIN), .in1(CPUDATAIN), .out(DATALE), .sel(LEDFEND));
  and and_3 (IOCS, ADDR[5], ADDR[6], ADDR[7], ADDR[8], ADDR[9], ADDR[10], ADDR[11], ADDR[12], ADDR[13], ADDR[14], 1'b1);
  and and_4 (TTYCS, IOCS, ADDR[0], ~ADDR[1], ~ADDR[2], ~ADDR[3], ADDR[4]);  // AND_Gate
  and and_5 (KBCS, IOCS, ~ADDR[0], ~ADDR[1], ~ADDR[2], ~ADDR[3], ADDR[4]);  // AND_Gate
  and and_6 (IVECTADDR, ADDR[0], ADDR[1], ADDR[2], ADDR[3], ADDR[4], ADDR[5], ADDR[6], ADDR[7], ADDR[8], ADDR[9], ADDR[10], ADDR[11], ADDR[12], ADDR[13], ADDR[14]);
  and and_7 (TTYWR, TTYCS, WE);
  and and_8 (and_8_out, TTYWR, DATA7);
  and and_9 (KBRD, KBCS, RE);
  and and_10 (and_10_out, KBCS, WE);
  Multiplexer #(.enable("false")) multiplexer_17 (.in0(and_10_out), .in1(1'b0), .out(multiplexer_17_out), .sel(KBCLR));
  and and_11 (LEDCS, IOCS, ~ADDR[4], RWE);  // AND_Gate
  and and_12 (IVECTEN, IVECTADDR, WE);
  and and_13 (IVECTRE, IVECTADDR, RE);
  or or_16 (RWE, RE, WE);
  and and_14 (MEMCS, ~IOCS, RWE);  // AND_Gate
  Multiplexer #(.enable("false")) multiplexer_18 (.in0(and_8_out), .in1(1'b0), .out(multiplexer_18_out), .sel(TTYCLR));
  D_Flip_Flop d_ff_1 (.clk(CLK), .D(multiplexer_17_out), .Q(KBCLR));  // open: Qn, preset, en, reset
  Register #(.width(15)) register_16 (.D(CPUDATAIN), .en(IVECTEN), .Q(IVECT), .clk(CLK));  // open: clr
  D_Flip_Flop d_ff_2 (.clk(CLK), .D(multiplexer_18_out), .Q(TTYCLR));  // open: Qn, preset, en, reset

  assign IRQ = KBIRQ;
  assign TTYDATA = CPUDATAIN[6:0];

  // Other names for the same wires on the sheet: DATA[14:0] = CPUDATAIN; KBDATA15[7:0] = {DATA7, KBDATA}
endmodule

module _15bAdder (
  input  [14:0] A,
  input  [14:0] B,
  input  Cin,
  output [14:0] C,
  output Cout
);

  wire _0__1_pout, _2_1_gout, _2_1_pout, _2__1_pout, _4_3_gout, _4_3_pout, _5_3_gout, _5_3_pout, _6_3_gout,
       _6_3_pout, _6_5_gout, _6_5_pout, _6__1_pout, _8_7_gout, _8_7_pout, _9_7_gout, _9_7_pout, _10_7_gout,
       _10_7_pout, _10_9_gout, _10_9_pout, _11_7_gout, _11_7_pout, _12_7_gout, _12_7_pout, _12_11_gout,
       _12_11_pout, _13_7_gout, _13_7_pout, _13_11_gout, _13_11_pout, and_14_out, and_15_out, D1, D2, D3, D4,
       D5, D6, D7, D8, D9, D10, D11, D12, D13, D14, G0, G1, G2, G3, G4, G5, G6, G7, G8, G9, G10, G11, G12,
       G13, or_14_out, P0, P1, P2, P3, P4, P5, P6, P7, P8, P9, P10, P11, P12, P13, xor_1_out, xor_2_out,
       xor_3_out, xor_7_out, xor_8_out, xor_9_out, xor_13_out, xor_14_out, xor_15_out, xor_19_out,
       xor_20_out, xor_21_out, xor_25_out, xor_26_out, xor_27_out;

  or or_1 (P0, A[0], B[0]);
  and and_1 (G0, A[0], B[0]);
  or or_2 (P8, A[8], B[8]);
  and and_2 (G8, A[8], B[8]);
  xor xor_1 (xor_1_out, A[0], B[0]);
  xor xor_2 (xor_2_out, A[5], B[5]);
  xor xor_3 (xor_3_out, A[10], B[10]);
  SubPrefix _12_11 (.P2(P11), .G2(G11), .P1(P12), .G1(G12), .Pout(_12_11_pout), .Gout(_12_11_gout));
  SubPrefix _13_11 (.P2(_12_11_pout), .G2(_12_11_gout), .P1(P13), .G1(G13), .Pout(_13_11_pout), .Gout(_13_11_gout));
  SubPrefix _13_7 (
    .P2(_10_7_pout), .G2(_10_7_gout), .P1(_13_11_pout), .G1(_13_11_gout), .Pout(_13_7_pout), .Gout(_13_7_gout));
  SubPrefix _12_7 (
    .P2(_10_7_pout), .G2(_10_7_gout), .P1(_12_11_pout), .G1(_12_11_gout), .Pout(_12_7_pout), .Gout(_12_7_gout));
  SubPrefix subprefix_1 (.P2(_6__1_pout), .G2(D7), .P1(_13_7_pout), .G1(_13_7_gout), .Gout(D14));  // open: Pout
  SubPrefix _12__1 (.P2(_6__1_pout), .G2(D7), .P1(_12_7_pout), .G1(_12_7_gout), .Gout(D13));  // open: Pout
  xor xor_4 (C[0], xor_1_out, Cin);
  xor xor_5 (C[5], xor_2_out, D5);
  xor xor_6 (C[10], xor_3_out, D10);
  or or_3 (P1, A[1], B[1]);
  and and_3 (G1, A[1], B[1]);
  or or_4 (P9, A[9], B[9]);
  and and_4 (G9, A[9], B[9]);
  SubPrefix _11_7 (.P2(_10_7_pout), .G2(_10_7_gout), .P1(P11), .G1(G11), .Pout(_11_7_pout), .Gout(_11_7_gout));
  SubPrefix _10_9 (.P2(P9), .G2(G9), .P1(P10), .G1(G10), .Pout(_10_9_pout), .Gout(_10_9_gout));
  SubPrefix _10_7 (
    .P2(_8_7_pout), .G2(_8_7_gout), .P1(_10_9_pout), .G1(_10_9_gout), .Pout(_10_7_pout), .Gout(_10_7_gout));
  SubPrefix _10__1 (.P2(_6__1_pout), .G2(D7), .P1(_10_7_pout), .G1(_10_7_gout), .Gout(D11));  // open: Pout
  SubPrefix _11__1 (.P2(_6__1_pout), .G2(D7), .P1(_11_7_pout), .G1(_11_7_gout), .Gout(D12));  // open: Pout
  xor xor_7 (xor_7_out, A[1], B[1]);
  xor xor_8 (xor_8_out, A[6], B[6]);
  xor xor_9 (xor_9_out, A[11], B[11]);
  or or_5 (P2, A[2], B[2]);
  and and_5 (G2, A[2], B[2]);
  or or_6 (P10, A[10], B[10]);
  and and_6 (G10, A[10], B[10]);
  SubPrefix _8_7 (.P2(P7), .G2(G7), .P1(P8), .G1(G8), .Pout(_8_7_pout), .Gout(_8_7_gout));
  SubPrefix _9_7 (.P2(_8_7_pout), .G2(_8_7_gout), .P1(P9), .G1(G9), .Pout(_9_7_pout), .Gout(_9_7_gout));
  SubPrefix _8__1 (.P2(_6__1_pout), .G2(D7), .P1(_8_7_pout), .G1(_8_7_gout), .Gout(D9));  // open: Pout
  SubPrefix _9__1 (.P2(_6__1_pout), .G2(D7), .P1(_9_7_pout), .G1(_9_7_gout), .Gout(D10));  // open: Pout
  xor xor_10 (C[1], xor_7_out, D1);
  xor xor_11 (C[6], xor_8_out, D6);
  xor xor_12 (C[11], xor_9_out, D11);
  SubPrefix _6_5 (.P2(P5), .G2(G5), .P1(P6), .G1(G6), .Pout(_6_5_pout), .Gout(_6_5_gout));
  SubPrefix _6_3 (.P2(_4_3_pout), .G2(_4_3_gout), .P1(_6_5_pout), .G1(_6_5_gout), .Pout(_6_3_pout), .Gout(_6_3_gout));
  SubPrefix _6__1 (.P2(_2__1_pout), .G2(D3), .P1(_6_3_pout), .G1(_6_3_gout), .Pout(_6__1_pout), .Gout(D7));
  SubPrefix _7__1 (.P2(_6__1_pout), .G2(D7), .P1(P7), .G1(G7), .Gout(D8));  // open: Pout
  or or_7 (P3, A[3], B[3]);
  and and_7 (G3, A[3], B[3]);
  or or_8 (P11, A[11], B[11]);
  and and_8 (G11, A[11], B[11]);
  SubPrefix _4_3 (.P2(P3), .G2(G3), .P1(P4), .G1(G4), .Pout(_4_3_pout), .Gout(_4_3_gout));
  SubPrefix _5_3 (.P2(_4_3_pout), .G2(_4_3_gout), .P1(P5), .G1(G5), .Pout(_5_3_pout), .Gout(_5_3_gout));
  SubPrefix _5__1 (.P2(_2__1_pout), .G2(D3), .P1(_5_3_pout), .G1(_5_3_gout), .Gout(D6));  // open: Pout
  xor xor_13 (xor_13_out, A[2], B[2]);
  xor xor_14 (xor_14_out, A[7], B[7]);
  xor xor_15 (xor_15_out, A[12], B[12]);
  SubPrefix _3__1 (.P2(_2__1_pout), .G2(D3), .P1(P3), .G1(G3), .Gout(D4));  // open: Pout
  SubPrefix _4__1 (.P2(_2__1_pout), .G2(D3), .P1(_4_3_pout), .G1(_4_3_gout), .Gout(D5));  // open: Pout
  xor xor_16 (C[2], xor_13_out, D2);
  xor xor_17 (C[7], xor_14_out, D7);
  xor xor_18 (C[12], xor_15_out, D12);
  or or_9 (P4, A[4], B[4]);
  and and_9 (G4, A[4], B[4]);
  or or_10 (P12, A[12], B[12]);
  and and_10 (G12, A[12], B[12]);
  SubPrefix _2_1 (.P2(P1), .G2(G1), .P1(P2), .G1(G2), .Pout(_2_1_pout), .Gout(_2_1_gout));
  SubPrefix _1__1 (.P2(_0__1_pout), .G2(D1), .P1(P1), .G1(G1), .Gout(D2));  // open: Pout
  SubPrefix _2__1 (.P2(_0__1_pout), .G2(D1), .P1(_2_1_pout), .G1(_2_1_gout), .Pout(_2__1_pout), .Gout(D3));
  SubPrefix _0__1 (.P2(Cin), .G2(Cin), .P1(P0), .G1(G0), .Pout(_0__1_pout), .Gout(D1));
  xor xor_19 (xor_19_out, A[3], B[3]);
  xor xor_20 (xor_20_out, A[8], B[8]);
  xor xor_21 (xor_21_out, A[13], B[13]);
  or or_11 (P5, A[5], B[5]);
  and and_11 (G5, A[5], B[5]);
  or or_12 (P13, A[13], B[13]);
  and and_12 (G13, A[13], B[13]);
  xor xor_22 (C[3], xor_19_out, D3);
  xor xor_23 (C[8], xor_20_out, D8);
  xor xor_24 (C[13], xor_21_out, D13);
  or or_13 (P6, A[6], B[6]);
  and and_13 (G6, A[6], B[6]);
  or or_14 (or_14_out, A[14], B[14]);
  and and_14 (and_14_out, A[14], B[14]);
  xor xor_25 (xor_25_out, A[4], B[4]);
  xor xor_26 (xor_26_out, A[9], B[9]);
  xor xor_27 (xor_27_out, A[14], B[14]);
  and and_15 (and_15_out, or_14_out, D14);
  xor xor_28 (C[4], xor_25_out, D4);
  xor xor_29 (C[9], xor_26_out, D9);
  xor xor_30 (C[14], xor_27_out, D14);
  or or_15 (P7, A[7], B[7]);
  and and_16 (G7, A[7], B[7]);
  or or_16 (Cout, and_15_out, and_14_out);

  // Other names for the same wires on the sheet: D0 = Cin
endmodule

module SubPrefix (
  input  P2,
  input  G2,
  input  P1,
  input  G1,
  output Pout,
  output Gout
);

  wire and_1_out;

  and and_1 (and_1_out, P1, G2);
  and and_2 (Pout, P2, P1);
  or or_1 (Gout, and_1_out, G1);
endmodule

module ALU (
  input  [14:0] SrcA,
  input  [14:0] SrcB,
  input  [3:0] ALUControl,
  input  Z,
  input  N,
  input  O,
  input  C,
  output [14:0] Output,
  output Zo,
  output No,
  output Oo,
  output Co
);

  wire and_1_out, and_2_out, and_3_out, and_4_out, and_6_out, Cadd, or_1_out, or_2_out;
  wire [14:0] and_5_out, multiplexer_2_out, n15badder_1_c, n15badder_2_c, nor_1_out, not_1_out, not_2_out,
       or_3_out, xor_1_out;

  and and_1 (and_1_out, SrcA[14], SrcB[14], ~Output[14]);  // AND_Gate
  or or_1 (or_1_out, and_1_out, and_2_out);
  and and_2 (and_2_out, ~SrcA[14], ~SrcB[14], Output[14]);  // AND_Gate
  assign not_1_out = ~SrcB;  // NOT_Gate not_1, 15 bits wide
  Multiplexer #(.select(4), .enable("false")) multiplexer_1 (
    .in0(N), .in1(N), .in2(Output[14]), .in3(Output[14]), .in4(Output[14]), .in5(Output[14]),
    .in6(Output[14]), .in7(Output[14]), .in8(Output[14]), .in9(Output[14]), .in10(Output[14]),
    .in11(Output[14]), .in12(Output[14]), .in13(Output[14]), .in14(N), .in15(N), .out(No), .sel(ALUControl));
  or or_2 (or_2_out, and_4_out, and_3_out);
  and and_3 (and_3_out, SrcA[14], ~SrcB[14], ~Output[14]);  // AND_Gate
  and and_4 (and_4_out, ~SrcA[14], SrcB[14], Output[14]);  // AND_Gate
  Multiplexer #(.width(15)) multiplexer_2 (
    .in0(SrcB), .in1(not_1_out), .out(multiplexer_2_out), .sel(ALUControl[2]));  // open: en
  _15bAdder u_15badder_1 (.A(SrcA), .B(multiplexer_2_out), .Cin(ALUControl[2]), .C(n15badder_1_c), .Cout(Cadd));
  assign and_5_out = SrcA & multiplexer_2_out;  // AND_Gate and_5, 15 bits wide
  assign or_3_out = SrcA | multiplexer_2_out;  // OR_Gate or_3, 15 bits wide
  assign xor_1_out = SrcA ^ multiplexer_2_out;  // XOR_Gate xor_1, 15 bits wide
  assign not_2_out = ~SrcA;  // NOT_Gate not_2, 15 bits wide
  Multiplexer #(.select(4), .enable("false")) multiplexer_3 (
    .in0(O), .in1(O), .in2(or_1_out), .in3(or_1_out), .in4(or_2_out), .in5(O), .in6(O), .in7(O), .in8(O),
    .in9(O), .in10(O), .in11(O), .in12(O), .in13(O), .in14(O), .in15(O), .out(Oo), .sel(ALUControl));
  _15bAdder u_15badder_2 (.A(not_2_out), .B({15{1'b0}}), .Cin(ALUControl[3]), .C(n15badder_2_c));  // open: Cout
  assign nor_1_out = ~(Output | {15{1'b0}});  // NOR_Gate nor_1, 15 bits wide
  and and_6 (and_6_out, nor_1_out[0], nor_1_out[1], nor_1_out[2], nor_1_out[3], nor_1_out[4], nor_1_out[5], nor_1_out[6], nor_1_out[7], nor_1_out[8], nor_1_out[9], nor_1_out[10], nor_1_out[11], nor_1_out[12], nor_1_out[13], nor_1_out[14]);
  Multiplexer #(.select(4), .enable("false")) multiplexer_4 (
    .in0(Z), .in1(Z), .in2(and_6_out), .in3(and_6_out), .in4(and_6_out), .in5(and_6_out), .in6(and_6_out),
    .in7(and_6_out), .in8(and_6_out), .in9(and_6_out), .in10(and_6_out), .in11(and_6_out), .in12(and_6_out),
    .in13(and_6_out), .in14(Z), .in15(Z), .out(Zo), .sel(ALUControl));
  Multiplexer #(.select(4), .width(15)) multiplexer_5 (
    .in0(SrcA), .in1(SrcA), .in2(n15badder_1_c), .in3(n15badder_1_c), .in4(n15badder_1_c), .in5(and_5_out),
    .in6(or_3_out), .in7(xor_1_out), .in8(not_2_out), .in9(n15badder_2_c), .in10({C, SrcA[14:1]}),
    .in11({SrcA[13:0], C}), .in12({{2{SrcA[14]}}, SrcA[13:1]}), .in13({SrcA[13:0], 1'b0}), .out(Output),
    .sel(ALUControl));  // open: in14, in15, en
  Multiplexer #(.select(4), .enable("false")) multiplexer_6 (
    .in0(C), .in1(C), .in2(Cadd), .in3(Cadd), .in4(Cadd), .in5(C), .in6(C), .in7(C), .in8(C), .in9(C),
    .in10(SrcA[0]), .in11(SrcA[14]), .in12(SrcA[0]), .in13(SrcA[14]), .in14(C), .in15(C), .out(Co),
    .sel(ALUControl));

  // Other names for the same wires on the sheet: A[14:0] = SrcA; CLR = SrcA[14]; CRL = SrcA[14]; CRR = SrcA[0];
  //   CSR = SrcA[0]; B[14:0] = SrcB; Sig = Output[14]
endmodule

module RegisterFile (
  input  WE,
  input  [2:0] A1,
  input  [2:0] A2,
  input  [2:0] A3,
  input  [14:0] WD,
  input  CLK,
  output [14:0] RD1,
  output [14:0] RD2
);

  wire and_1_out, and_2_out, and_3_out, and_4_out, and_5_out, and_6_out, and_7_out, and_8_out,
       decoder_1_out0, decoder_1_out1, decoder_1_out2, decoder_1_out3, decoder_1_out4, decoder_1_out5,
       decoder_1_out6, decoder_1_out7;
  wire [14:0] register_1_q, register_2_q, register_3_q, register_4_q, register_5_q, register_6_q,
       register_7_q, register_8_q;

  Decoder #(.select(3), .enable("false")) decoder_1 (
    .out0(decoder_1_out0), .out1(decoder_1_out1), .out2(decoder_1_out2), .out3(decoder_1_out3),
    .out4(decoder_1_out4), .out5(decoder_1_out5), .out6(decoder_1_out6), .out7(decoder_1_out7), .sel(A3));
  and and_1 (and_1_out, WE, decoder_1_out0);
  and and_2 (and_2_out, WE, decoder_1_out1);
  and and_3 (and_3_out, WE, decoder_1_out2);
  and and_4 (and_4_out, WE, decoder_1_out3);
  and and_5 (and_5_out, WE, decoder_1_out4);
  and and_6 (and_6_out, WE, decoder_1_out5);
  and and_7 (and_7_out, WE, decoder_1_out6);
  and and_8 (and_8_out, WE, decoder_1_out7);
  Register #(.width(15)) register_1 (.D(WD), .en(and_1_out), .Q(register_1_q), .clk(CLK));  // open: clr
  Register #(.width(15)) register_2 (.D(WD), .en(and_2_out), .Q(register_2_q), .clk(CLK));  // open: clr
  Register #(.width(15)) register_3 (.D(WD), .en(and_3_out), .Q(register_3_q), .clk(CLK));  // open: clr
  Register #(.width(15)) register_4 (.D(WD), .en(and_4_out), .Q(register_4_q), .clk(CLK));  // open: clr
  Register #(.width(15)) register_5 (.D(WD), .en(and_5_out), .Q(register_5_q), .clk(CLK));  // open: clr
  Register #(.width(15)) register_6 (.D(WD), .en(and_6_out), .Q(register_6_q), .clk(CLK));  // open: clr
  Register #(.width(15)) register_7 (.D(WD), .en(and_7_out), .Q(register_7_q), .clk(CLK));  // open: clr
  Register #(.width(15)) register_8 (.D(WD), .en(and_8_out), .Q(register_8_q), .clk(CLK));  // open: clr
  Multiplexer #(.select(3), .width(15)) multiplexer_1 (
    .in0(register_1_q), .in1(register_2_q), .in2(register_3_q), .in3(register_4_q), .in4(register_5_q),
    .in5(register_6_q), .in6(register_7_q), .in7(register_8_q), .out(RD1), .sel(A1));  // open: en
  Multiplexer #(.select(3), .width(15)) multiplexer_2 (
    .in0(register_1_q), .in1(register_2_q), .in2(register_3_q), .in3(register_4_q), .in4(register_5_q),
    .in5(register_6_q), .in6(register_7_q), .in7(register_8_q), .out(RD2), .sel(A2));  // open: en
endmodule
